// Logisim project CSE_Project.circ as structural Verilog
module Reg_file (
  input  [9:0] in_1,
  input  in_2,
  input  in_3,
  input  [1:0] in_4,
  input  [1:0] in_5,
  input  [1:0] in_6,
  output [9:0] out_7,
  output [9:0] out_8
);

  wire demultiplexer_1_out0, demultiplexer_1_out1, demultiplexer_1_out2, demultiplexer_1_out3;
  wire [9:0] register_1_q, register_2_q, register_3_q, register_4_q;

  Demultiplexer #(.select(2)) demultiplexer_1 (
    .out0(demultiplexer_1_out0), .out1(demultiplexer_1_out1), .out2(demultiplexer_1_out2),
    .out3(demultiplexer_1_out3), .in(in_2), .sel(in_5));
  Register #(.width(10)) register_1 (.D(in_1), .en(demultiplexer_1_out0), .Q(register_1_q), .clk(in_3));  // open: clr
  Register #(.width(10)) register_2 (.D(in_1), .en(demultiplexer_1_out1), .Q(register_2_q), .clk(in_3));  // open: clr
  Register #(.width(10)) register_3 (.D(in_1), .en(demultiplexer_1_out2), .Q(register_3_q), .clk(in_3));  // open: clr
  Register #(.width(10)) register_4 (.D(in_1), .en(demultiplexer_1_out3), .Q(register_4_q), .clk(in_3));  // open: clr
  Multiplexer #(.select(2), .width(10)) multiplexer_1 (
    .in0(register_1_q), .in1(register_2_q), .in2(register_3_q), .in3(register_4_q), .out(out_7), .sel(in_4));
  Multiplexer #(.select(2), .width(10)) multiplexer_2 (
    .in0(register_1_q), .in1(register_2_q), .in2(register_3_q), .in3(register_4_q), .out(out_8), .sel(in_6));
endmodule

module ALU_1_Bit (
  input  A,
  input  B,
  input  Cin,
  input  Binvert,
  input  [1:0] in_5,
  output cout,
  output Result
);

  wire adder_1_out, and_1_out, multiplexer_1_out, not_1_out, or_1_out;

  Multiplexer multiplexer_1 (.in0(B), .in1(not_1_out), .out(multiplexer_1_out), .sel(Binvert));
  not not_1 (not_1_out, B);
  Adder #(.width(1)) adder_1 (.a(multiplexer_1_out), .b(A), .out(adder_1_out), .cin(Cin), .cout(cout));
  and and_1 (and_1_out, A, multiplexer_1_out);
  or or_1 (or_1_out, A, multiplexer_1_out);
  Multiplexer #(.select(2)) multiplexer_2 (
    .in0(adder_1_out), .in1(and_1_out), .in2(or_1_out), .out(Result), .sel(in_5));  // open: in3
endmodule

module Datapath (
  output [3:0] Opcode,
  output [1:0] RS,
  output [1:0] RT,
  output [1:0] imm,
  output [9:0] Data1,
  output [9:0] Data2,
  output [9:0] Result,
  output [9:0] out_8,
  output [9:0] Data_For_Store
);

  wire alu_10_buit_1_zero, and_1_out, clock_1_out, control_unit_1_alu_src, control_unit_1_beq,
       control_unit_1_jump, control_unit_1_lw, control_unit_1_ram_to_reg, control_unit_1_reg_dest,
       control_unit_1_sub, control_unit_1_sw, control_unit_1_wr_enable;
  wire [1:0] control_unit_1_alu_op, multiplexer_1_out;
  wire [9:0] adder_1_out, adder_2_out, bit_extender_1_out, multiplexer_3_out, multiplexer_4_out, ram_1_dout,
       register_1_q;
  wire [9:6] undriven;

  Control_Unit control_unit_1 (
    .Wr_Enable(control_unit_1_wr_enable), .ALU_Op(control_unit_1_alu_op), .ALU_Src(control_unit_1_alu_src),
    .Sub(control_unit_1_sub), .SW(control_unit_1_sw), .LW(control_unit_1_lw),
    .RAM_To_Reg(control_unit_1_ram_to_reg), .Jump(control_unit_1_jump), .Beq(control_unit_1_beq),
    .Reg_Dest(control_unit_1_reg_dest), .Opcode(Opcode));
  Register #(.width(10)) register_1 (.D(multiplexer_4_out), .Q(register_1_q), .clk(clock_1_out));  // open: en, clr
  Clock clock_1 (.out(clock_1_out));
  Adder #(.width(10)) adder_1 (.a(10'h1), .b(register_1_q), .out(adder_1_out));  // open: cin, cout
  ROM #(.addrWidth(10), .dataWidth(10)) rom_1 (.addr(register_1_q), .data({Opcode, RS, RT, imm}));
  assign bit_extender_1_out = {{8{imm[1]}}, imm};  // Bit_Extender bit_extender_1
  Reg_file reg_file_1 (
    .out_8(Data_For_Store), .out_7(Data1), .in_1(out_8), .in_2(control_unit_1_wr_enable), .in_3(clock_1_out),
    .in_5(multiplexer_1_out), .in_4(RS), .in_6(RT));
  Multiplexer #(.enable("true"), .width(2)) multiplexer_1 (
    .in0(imm), .in1(RT), .out(multiplexer_1_out), .sel(control_unit_1_reg_dest));  // open: en
  Multiplexer #(.enable("true"), .width(10)) multiplexer_2 (
    .in0(Data_For_Store), .in1(bit_extender_1_out), .out(Data2), .sel(control_unit_1_alu_src));  // open: en
  ALU_10_buit alu_10_buit_1 (
    .Result(Result), .ZERO(alu_10_buit_1_zero), .OP(control_unit_1_alu_op), .A(Data1), .B(Data2),
    .Cin(control_unit_1_sub), .Binvert(control_unit_1_sub));  // open: overflow, Cout
  Multiplexer #(.enable("true"), .width(10)) multiplexer_3 (
    .in0(adder_1_out), .in1(adder_2_out), .out(multiplexer_3_out), .sel(and_1_out));  // open: en
  Adder #(.width(10)) adder_2 (.a(adder_1_out), .b(bit_extender_1_out), .out(adder_2_out));  // open: cin, cout
  and and_1 (and_1_out, alu_10_buit_1_zero, control_unit_1_beq);
  Multiplexer #(.enable("true"), .width(10)) multiplexer_4 (
    .in0(multiplexer_3_out), .in1({undriven, RS, RT, imm}), .out(multiplexer_4_out), .sel(control_unit_1_jump));  // open: en
  RAM #(.addrWidth(10), .dataWidth(10)) ram_1 (
    .addr(Result), .we(control_unit_1_sw), .oe(control_unit_1_lw), .clk(clock_1_out), .din(Data_For_Store),
    .dout(ram_1_dout));
  Multiplexer #(.enable("true"), .width(10)) multiplexer_5 (
    .in0(Result), .in1(ram_1_dout), .out(out_8), .sel(control_unit_1_ram_to_reg));  // open: en

  // Notes on the sheet:
  //   contents of rom_1 (hex, n*v repeats v):
  //   123 23 12 221 212
endmodule

module ALU_10_buit (
  input  [9:0] A,
  input  [1:0] OP,
  input  Binvert,
  input  Cin,
  input  [9:0] B,
  output [9:0] Result,
  output ZERO,
  output overflow,
  output Cout
);

  wire alu_1_bit_1_cout, alu_1_bit_2_cout, alu_1_bit_3_cout, alu_1_bit_4_cout, alu_1_bit_5_cout,
       alu_1_bit_6_cout, alu_1_bit_7_cout, alu_1_bit_8_cout, alu_1_bit_10_cout;

  ALU_1_Bit alu_1_bit_1 (
    .Result(Result[1]), .cout(alu_1_bit_1_cout), .in_5(OP), .A(A[0]), .B(B[1]), .Cin(alu_1_bit_10_cout));  // open: Binvert
  ALU_1_Bit alu_1_bit_2 (
    .Result(Result[2]), .cout(alu_1_bit_2_cout), .in_5(OP), .A(A[2]), .B(B[2]), .Binvert(Binvert),
    .Cin(alu_1_bit_1_cout));
  ALU_1_Bit alu_1_bit_3 (
    .Result(Result[3]), .cout(alu_1_bit_3_cout), .in_5(OP), .A(A[3]), .B(B[3]), .Binvert(Binvert),
    .Cin(alu_1_bit_2_cout));
  ALU_1_Bit alu_1_bit_4 (
    .Result(Result[4]), .cout(alu_1_bit_4_cout), .in_5(OP), .A(A[4]), .B(B[4]), .Binvert(Binvert),
    .Cin(alu_1_bit_3_cout));
  ALU_1_Bit alu_1_bit_5 (
    .Result(Result[5]), .cout(alu_1_bit_5_cout), .in_5(OP), .A(A[5]), .B(B[5]), .Binvert(Binvert),
    .Cin(alu_1_bit_4_cout));
  ALU_1_Bit alu_1_bit_6 (
    .Result(Result[6]), .cout(alu_1_bit_6_cout), .in_5(OP), .A(A[6]), .B(B[6]), .Binvert(Binvert),
    .Cin(alu_1_bit_5_cout));
  ALU_1_Bit alu_1_bit_7 (
    .Result(Result[7]), .cout(alu_1_bit_7_cout), .in_5(OP), .A(A[7]), .B(B[7]), .Binvert(Binvert),
    .Cin(alu_1_bit_6_cout));
  ALU_1_Bit alu_1_bit_8 (
    .Result(Result[8]), .cout(alu_1_bit_8_cout), .in_5(OP), .A(A[8]), .B(B[8]), .Binvert(Binvert),
    .Cin(alu_1_bit_7_cout));
  ALU_1_Bit alu_1_bit_9 (
    .Result(Result[9]), .cout(Cout), .in_5(OP), .A(A[9]), .B(B[9]), .Binvert(Binvert), .Cin(alu_1_bit_8_cout));
  ALU_1_Bit alu_1_bit_10 (
    .Result(Result[0]), .cout(alu_1_bit_10_cout), .in_5(OP), .A(A[1]), .B(B[0]), .Binvert(Binvert), .Cin(Cin));
  xor xor_1 (overflow, alu_1_bit_8_cout, Cout);
  nor nor_1 (ZERO, Result[0], Result[1], Result[2], Result[3], Result[4], Result[5], Result[6], Result[7], Result[8], Result[9]);
endmodule

module Control_Unit (
  input  [3:0] Opcode,
  output Reg_Dest,
  output Wr_Enable,
  output [1:0] ALU_Op,
  output ALU_Src,
  output Sub,
  output SW,
  output LW,
  output RAM_To_Reg,
  output Jump,
  output Beq
);

  wire and_1_out, and_2_out, and_3_out, and_4_out, and_5_out, and_8_out, and_9_out, and_10_out, and_11_out,
       and_16_out, and_17_out, not_1_out, not_2_out, not_3_out, not_4_out;

  not not_1 (not_1_out, Opcode[3]);
  not not_2 (not_2_out, Opcode[2]);
  not not_3 (not_3_out, Opcode[1]);
  not not_4 (not_4_out, Opcode[0]);
  and and_1 (and_1_out, not_1_out, not_2_out, Opcode[1], not_4_out);
  and and_2 (and_2_out, Opcode[3], not_2_out, not_3_out, not_4_out);
  and and_3 (and_3_out, not_1_out, not_2_out);
  and and_4 (and_4_out, not_1_out, not_3_out, not_4_out);
  and and_5 (and_5_out, not_2_out, not_3_out, not_4_out);
  and and_6 (ALU_Op[1], not_1_out, Opcode[2], not_3_out, not_4_out);
  and and_7 (ALU_Op[0], not_1_out, not_2_out, Opcode[1], Opcode[0]);
  and and_8 (and_8_out, not_1_out, not_2_out, Opcode[1], not_4_out);
  and and_9 (and_9_out, Opcode[3], not_2_out, not_3_out);
  and and_10 (and_10_out, not_1_out, not_3_out, Opcode[0]);
  and and_11 (and_11_out, not_1_out, Opcode[2], Opcode[1], not_4_out);
  and and_12 (SW, Opcode[3], not_2_out, not_3_out, Opcode[0]);
  and and_13 (LW, Opcode[3], not_2_out, not_3_out, not_4_out);
  and and_14 (RAM_To_Reg, Opcode[3], not_2_out, not_3_out, not_4_out);
  and and_15 (Jump, not_1_out, Opcode[2], Opcode[1], Opcode[0]);
  and and_16 (and_16_out, not_1_out, Opcode[2], not_3_out, Opcode[0]);
  and and_17 (and_17_out, not_1_out, Opcode[2], Opcode[1], not_4_out);
  or or_1 (Reg_Dest, and_1_out, and_2_out);
  or or_2 (Wr_Enable, and_3_out, and_4_out, and_5_out);
  or or_3 (ALU_Src, and_8_out, and_9_out);
  or or_4 (Sub, and_10_out, and_11_out);
  or or_5 (Beq, and_16_out, and_17_out);
endmodule
